# Fritzing sketch PlantPumpPCB (saved by Fritzing 0.9.3b)
breadboards: 1

parts:
  Part1 = Arduino Pro Mini v13
  Q1 = Basic FET N-Channel [package="TO220 [THT]"]
  D1 = Rectifier Diode [part_number=1N4001 package="300 mil [THT]"]
  U2 = Mystery Part - 4 pins [chip_label="Inibud DC-DC StepUp" package=THT]
  VCC1 = Battery
  M2 = DC Motor
  Step-Up/Reg_3_3V1 = female alternating pin header, 4 pins [form="♀ (female)"]
  nRF24L2 = NRF24L01+ Breakout Board
  C3 = Electrolytic Capacitor [capacitance=10µF package="100 mil [THT, electrolytic]"]
  R1 = Resistor [tolerance=±5% resistance=330 package=THT]

nets (from the breadboard view):
  N1: Part1.RAW, U2.IN+, Step-Up/Reg_3_3V1.pin4, nRF24L2.VCC, C3.+
  GND: Part1.GND, Q1.source, U2.IN-, U2.OUT-, VCC1.-, Step-Up/Reg_3_3V1.pin3, nRF24L2.GND, C3.-
  N2: Part1.D13/SCK, nRF24L2.SCK
  N3: Part1.D12/MISO, nRF24L2.MISO
  N4: Part1.D11_PWM/MOSI, nRF24L2.MOSI
  N5: Part1.D10_PWM/SS, nRF24L2.CS
  N6: Part1.D9_PWM, R1.Pin_0
  N7: Part1.D6_PWM, nRF24L2.CE
  N8: Q1.gate, R1.Pin_1
  N9: Q1.drain, D1.cathode, M2.pin_1
  N10: D1.anode, U2.OUT+, M2.pin_2
  N11: VCC1.+, Step-Up/Reg_3_3V1.pin2

notes:
  MISO:12 - SCK:13 - CE:6 - GND
  BULK - MOSI:11 - CS:10 - VCC

custom parts:
  Mystery Part - 4 pins: A dummy, proxy, ersatz, stand-in part for whatever you want. With 4 pins on a 600mil inline pin header footprint.
