# Fritzing sketch PlantPumpPCB01 (saved by Fritzing 0.9.3b)
breadboards: 1

parts:
  Part1 = Arduino Pro Mini v13
  Q1 = Basic FET N-Channel [package="TO220 [THT]"]
  D1 = Rectifier Diode [part_number=1N4001 package="300 mil [THT]"]  # not connected
  VCC1 = Battery
  Step-Up/Reg_3_3V1 = female alternating pin header, 4 pins [form="♀ (female)"]
  nRF24L2 = NRF24L01+ Breakout Board
  C3 = Electrolytic Capacitor [capacitance=10µF package="100 mil [THT, electrolytic]"]
  Power_plug1 = Power plug  # not connected
  M2 = DC Motor

nets (from the breadboard view):
  N1: Part1.RAW, Step-Up/Reg_3_3V1.pin1, nRF24L2.VCC, C3.-
  GND: Part1.GND, VCC1.-, Step-Up/Reg_3_3V1.pin2, nRF24L2.GND, C3.+
  N2: Part1.D13/SCK, nRF24L2.SCK
  N3: Part1.D12/MISO, nRF24L2.MISO
  N4: Part1.D11_PWM/MOSI, nRF24L2.MOSI
  N5: Part1.D10_PWM/SS, nRF24L2.CS
  N6: Part1.D9_PWM, Q1.gate
  N7: Part1.D6_PWM, nRF24L2.CE
  N8: Q1.drain, M2.pin_2
  N9: VCC1.+, Step-Up/Reg_3_3V1.pin3

notes:
  MISO:12 - SCK:13 - CE:6 - GND
  INT:2 - MOSI:11 - CS:10 - VCC
