# Fritzing sketch PlantSensorPCB10 (saved by Fritzing 0.9.3b)
circuit board: 5.50183cm x 4.60217cm
breadboards: 1

parts:
  C2 = Electrolytic Capacitor [capacitance=10µF package="100 mil [THT, electrolytic]"]
  C1 = Electrolytic Capacitor [capacitance=10µF package="100 mil [THT, electrolytic]"]
  J2 = Screw terminal - 2 pins [package=THT]
  R1 = Resistor [tolerance=±5% resistance=22k package=THT]
  R2 = Resistor [tolerance=±5% resistance=1M package=THT]
  R3 = Resistor [tolerance=±5% resistance=470k package=THT]
  R4 = Resistor [tolerance=±5% resistance=39k package=THT]
  R5 = Resistor [tolerance=±5% resistance=1M package=THT]
  R6 = Resistor [tolerance=±5% resistance=3.2k package=THT]
  R7 = Resistor [tolerance=±5% resistance=1.2k package=THT]
  PhotoResistor = PHOTOCELL [package=photocell]
  Arduino_Pro_Mini_3_3_V = Arduino Pro Mini (3.3V)
  Step-Up/Reg_3_3V = female pin header, 4 pins [form="♀ (female)"]
  nRF24L01 = NRF24L01+ Breakout Board
  DHT1_-_Humidity/Sensor = male pin header, 3 pins [form="♂ (male)"]
  Arduino_Programmer = male pin header, 6 pins [form="♂ (male)"]
  Moisture_Sensor_1 = female pin header, 3 pins [form="♀ (female)"]
  Moisture_Sensor_2 = female pin header, 3 pins [form="♀ (female)"]
  C3 = Ceramic Capacitor [capacitance=100nF package="100 mil [THT, multilayer]"]
  Real_Time_Clock = female pin header, 6 pins [form="♀ (female)"]
  Jumper_1 = male pin header, 2 pins [form="♂ (male)"]
  Jumper_2 = male pin header, 1 pin [form="♂ (male)"]

nets:
  GND: C2.-, C1.-, J2.pin1, R1.Pin_1, R7.Pin_0, Arduino_Pro_Mini_3_3_V.GND, Step-Up/Reg_3_3V.pin2, nRF24L01.GND, DHT1_-_Humidity/Sensor.pin1, Arduino_Programmer.pin1, Arduino_Programmer.pin2, Moisture_Sensor_1.pin3, Moisture_Sensor_2.pin3, C3.0, Real_Time_Clock.pin6
  VCC: C2.+, Arduino_Pro_Mini_3_3_V.VCC, Step-Up/Reg_3_3V.pin1, nRF24L01.VCC, Arduino_Programmer.pin3, C3.1, Real_Time_Clock.pin5
  N1: C1.+, J2.pin2, R5.Pin_1, Step-Up/Reg_3_3V.pin3
  N2: R1.Pin_0, R2.Pin_0, R3.Pin_0
  N3: R2.Pin_1, R3.Pin_1, R4.Pin_0
  N4: R4.Pin_1, R5.Pin_0, Arduino_Pro_Mini_3_3_V.A0
  N5: R6.Pin_0, DHT1_-_Humidity/Sensor.pin3, Moisture_Sensor_1.pin2, Moisture_Sensor_2.pin2, Jumper_1.pin1, Jumper_2.pin1
  N6: R6.Pin_1, PhotoResistor.P$2
  N7: R7.Pin_1, PhotoResistor.P$1, Arduino_Pro_Mini_3_3_V.A1
  N8: Arduino_Pro_Mini_3_3_V.DTR, Arduino_Programmer.pin6
  N9: Arduino_Pro_Mini_3_3_V.TXO, Arduino_Programmer.pin5
  N10: Arduino_Pro_Mini_3_3_V.RXI, Arduino_Programmer.pin4
  N11: Arduino_Pro_Mini_3_3_V.A4, Real_Time_Clock.pin4
  N12: Arduino_Pro_Mini_3_3_V.A5, Real_Time_Clock.pin3
  N13: Arduino_Pro_Mini_3_3_V.A3, Moisture_Sensor_2.pin1
  N14: Arduino_Pro_Mini_3_3_V.A2, Moisture_Sensor_1.pin1
  N15: Arduino_Pro_Mini_3_3_V.SCK, nRF24L01.SCK
  N16: Arduino_Pro_Mini_3_3_V.MISO, nRF24L01.MISO
  N17: Arduino_Pro_Mini_3_3_V.MOSI, nRF24L01.MOSI
  N18: Arduino_Pro_Mini_3_3_V.D10, nRF24L01.CS
  N19: Arduino_Pro_Mini_3_3_V.D9, nRF24L01.CE
  N20: Arduino_Pro_Mini_3_3_V.D8, Jumper_1.pin2
  N21: Arduino_Pro_Mini_3_3_V.D5, DHT1_-_Humidity/Sensor.pin2
  N22: Arduino_Pro_Mini_3_3_V.D3, Real_Time_Clock.pin1
  N23: Arduino_Pro_Mini_3_3_V.D2, Real_Time_Clock.pin2

notes:
  Battery Consumption
  https://www.mysensors.org/build/battery
  V_Out = (R_2 / (R_1 + R_2)) V_in
  V_in = 1.34 * 2 = 2.68 V
  V_Out is the voltage of reference is 1.1 V
  1.1 V = (R_2 / (R_1 + R_2)) 2.68 V
  1.1 V * (R_1 + R_2)/R_2 = 2.68 V
  1.1 V * (1 + R_1/R_2) = 2.68 V
  1.1 V + 1.1 V * (R_1/R_2) = 2.68 V
  2.68 V - 1.1 V = 1.58 V
  R_1/R_2 = 1.58 V / 1.1 V
  Battery Sensor
  (Input V Max 4V)
  Light Sensor
  Voltage Regulator
  PCB designed by Ezio Bartocci
  for the Project of NES 2016
